// Logisim project Snap_Game.circ as structural Verilog: 14 circuits, main circuit Computer
module Computer (
);

  wire clock_1_out;
  wire [7:0] cpu3_1_control, cpu3_1_screen__x, cpu3_1_screen__y, screendecoder_1_output_0,
       screendecoder_1_output_1, screendecoder_1_output_2, screendecoder_1_output_4,
       screendecoder_1_output_5, screendecoder_1_output_6, screendecoder_1_output_7;
  wire [31:24] screendecoder_1_output_3;

  Clock clock_1 (.out(clock_1_out));
  DotMatrix #(.matrixcols(8), .matrixrows(8), .persist(1)) dotmatrix_1 (
    .col0(screendecoder_1_output_0), .col1(screendecoder_1_output_1), .col2(screendecoder_1_output_2),
    .col3(screendecoder_1_output_3), .col4(screendecoder_1_output_4), .col5(screendecoder_1_output_5),
    .col6(screendecoder_1_output_6), .col7(screendecoder_1_output_7));
  CPU3 cpu3_1 (
    .Clock(clock_1_out), .Screen__x(cpu3_1_screen__x), .Screen__y(cpu3_1_screen__y), .Control(cpu3_1_control));
  ScreenDecoder screendecoder_1 (
    .Input_y_label(cpu3_1_screen__y), .Input_x_label(cpu3_1_screen__x), .Clock(cpu3_1_control[2]),
    .Falsh(cpu3_1_control[1]), .Clear(cpu3_1_control[0]), .Output_0(screendecoder_1_output_0),
    .Output_1(screendecoder_1_output_1), .Output_2(screendecoder_1_output_2),
    .Output_3(screendecoder_1_output_3), .Output_4(screendecoder_1_output_4),
    .Output_5(screendecoder_1_output_5), .Output_6(screendecoder_1_output_6),
    .Output_7(screendecoder_1_output_7));
endmodule

module AU (
  input  Control__1_add__0_subtract,
  input  [7:0] The_number_awaiting_calculation,
  input  [7:0] The_number_awaiting_calculation_2,
  output [7:0] Calculation_results
);

  wire [7:0] adder_1_out, subtractor_1_out;

  Subtractor subtractor_1 (
    .a(The_number_awaiting_calculation), .b(The_number_awaiting_calculation_2), .out(subtractor_1_out));  // open: bin, bout
  Adder adder_1 (
    .a(The_number_awaiting_calculation), .b(The_number_awaiting_calculation_2), .out(adder_1_out));  // open: cin, cout
  Multiplexer #(.width(8), .enable("false")) multiplexer_1 (
    .in0(subtractor_1_out), .in1(adder_1_out), .out(Calculation_results), .sel(Control__1_add__0_subtract));
endmodule

module LU (
  input  Control__1_AND__0_OR,
  input  [7:0] Input_0,
  input  [7:0] Input_1,
  output [7:0] out_4
);

  wire [7:0] and_1_out, or_1_out;

  assign or_1_out = Input_0 | Input_1;  // OR_Gate or_1, 8 bits wide
  assign and_1_out = Input_0 & Input_1;  // AND_Gate and_1, 8 bits wide
  Multiplexer #(.width(8), .enable("false")) multiplexer_1 (
    .in0(or_1_out), .in1(and_1_out), .out(out_4), .sel(Control__1_AND__0_OR));
endmodule

module ALU (
  input  [2:0] Control__100x_LU__011x_AU,
  input  [7:0] Data__input_number,
  input  [7:0] Data__input_number_2,
  output [7:0] Data__output_number
);

  wire [7:0] au_1_calculation_results, lu_1_out_4;

  LU lu_1 (
    .Control__1_AND__0_OR(Control__100x_LU__011x_AU[0]), .Input_1(Data__input_number_2), .out_4(lu_1_out_4),
    .Input_0(Data__input_number));
  AU au_1 (
    .Calculation_results(au_1_calculation_results),
    .Control__1_add__0_subtract(Control__100x_LU__011x_AU[1]),
    .The_number_awaiting_calculation(Data__input_number),
    .The_number_awaiting_calculation_2(Data__input_number_2));
  Multiplexer #(.width(8), .enable("false")) multiplexer_1 (
    .in0(lu_1_out_4), .in1(au_1_calculation_results), .out(Data__output_number),
    .sel(Control__100x_LU__011x_AU[2]));
endmodule

// PC
module PC1 (
  input  Clock__time_counter,
  output [7:0] Data__total_time
);

  wire [7:0] adder_1_out;

  Register register_1 (.D(adder_1_out), .Q(Data__total_time), .clk(Clock__time_counter));  // open: en, clr
  Adder adder_1 (.a(Data__total_time), .b(8'h1), .out(adder_1_out));  // open: cin, cout
endmodule

// PC
module PC2 (
  input  [7:0] Jump_position,
  input  Jump__1_jump__2_normal,
  input  Clock__time_counter,
  output [7:0] Data__total_time
);

  wire [7:0] adder_1_out, multiplexer_1_out;

  Multiplexer #(.width(8), .enable("false")) multiplexer_1 (
    .in0(adder_1_out), .in1(Jump_position), .out(multiplexer_1_out), .sel(Jump__1_jump__2_normal));
  Register register_1 (.D(multiplexer_1_out), .Q(Data__total_time), .clk(Clock__time_counter));  // open: en, clr
  Adder adder_1 (.a(Data__total_time), .b(8'h1), .out(adder_1_out));  // open: cin, cout
endmodule

// Register Group
module RegisterGroup1 (
  input  [7:0] Data__to_be_written,
  input  [4:0] Address__to_be_read,
  input  [4:0] Address__to_be_written,
  input  Enable__Written,
  input  Clock__value_update_on_trigger,
  output [7:0] Data__to_be_output
);

  wire and_1_out, and_2_out, and_3_out, and_4_out, and_5_out, and_6_out, and_7_out, and_8_out,
       decoder_1_out0, decoder_1_out1, decoder_1_out2, decoder_1_out3, decoder_1_out4, decoder_1_out5,
       decoder_1_out6, decoder_1_out7;
  wire [7:0] register_1_q, register_2_q, register_3_q, register_4_q, register_5_q, register_6_q,
       register_7_q, register_8_q;

  Decoder #(.select(3), .enable("false")) decoder_1 (
    .out0(decoder_1_out0), .out1(decoder_1_out1), .out2(decoder_1_out2), .out3(decoder_1_out3),
    .out4(decoder_1_out4), .out5(decoder_1_out5), .out6(decoder_1_out6), .out7(decoder_1_out7),
    .sel(Address__to_be_written[2:0]));
  and and_1 (and_1_out, decoder_1_out0, Enable__Written);
  and and_2 (and_2_out, decoder_1_out1, Enable__Written);
  and and_3 (and_3_out, decoder_1_out2, Enable__Written);
  and and_4 (and_4_out, decoder_1_out3, Enable__Written);
  and and_5 (and_5_out, decoder_1_out4, Enable__Written);
  and and_6 (and_6_out, decoder_1_out5, Enable__Written);
  and and_7 (and_7_out, decoder_1_out6, Enable__Written);
  and and_8 (and_8_out, decoder_1_out7, Enable__Written);
  Register register_1 (
    .D(Data__to_be_written), .en(and_1_out), .Q(register_1_q), .clk(Clock__value_update_on_trigger));  // open: clr
  Register register_2 (
    .D(Data__to_be_written), .en(and_2_out), .Q(register_2_q), .clk(Clock__value_update_on_trigger));  // open: clr
  Register register_3 (
    .D(Data__to_be_written), .en(and_3_out), .Q(register_3_q), .clk(Clock__value_update_on_trigger));  // open: clr
  Register register_4 (
    .D(Data__to_be_written), .en(and_4_out), .Q(register_4_q), .clk(Clock__value_update_on_trigger));  // open: clr
  Register register_5 (
    .D(Data__to_be_written), .en(and_5_out), .Q(register_5_q), .clk(Clock__value_update_on_trigger));  // open: clr
  Register register_6 (
    .D(Data__to_be_written), .en(and_6_out), .Q(register_6_q), .clk(Clock__value_update_on_trigger));  // open: clr
  Register register_7 (
    .D(Data__to_be_written), .en(and_7_out), .Q(register_7_q), .clk(Clock__value_update_on_trigger));  // open: clr
  Register register_8 (.D(Data__to_be_written), .en(and_8_out), .Q(register_8_q));  // open: clk, clr
  Multiplexer #(.select(3), .width(8), .enable("false")) multiplexer_1 (
    .in0(register_1_q), .in1(register_2_q), .in2(register_3_q), .in3(register_4_q), .in4(register_5_q),
    .in5(register_6_q), .in6(register_7_q), .in7(register_8_q), .out(Data__to_be_output),
    .sel({Address__to_be_read[1], Address__to_be_read[2], Address__to_be_read[0]}));
endmodule

// Register Group
module RegisterGroup2 (
  input  [7:0] Data__to_be_written,
  input  [4:0] Address__to_be_read0,
  input  [4:0] Address__to_be_read1,
  input  [4:0] Address__to_be_written,
  input  Enable__Written,
  input  Clock__value_update_on_trigger,
  output [7:0] Data__to_be_output0,
  output [7:0] Data__to_be_output1
);

  wire and_1_out, and_2_out, and_3_out, and_4_out, and_5_out, and_6_out, and_7_out, and_8_out,
       decoder_1_out0, decoder_1_out1, decoder_1_out2, decoder_1_out3, decoder_1_out4, decoder_1_out5,
       decoder_1_out6, decoder_1_out7;
  wire [7:0] register_1_q, register_2_q, register_3_q, register_4_q, register_5_q, register_6_q,
       register_7_q, register_8_q;

  Decoder #(.select(3), .enable("false")) decoder_1 (
    .out0(decoder_1_out0), .out1(decoder_1_out1), .out2(decoder_1_out2), .out3(decoder_1_out3),
    .out4(decoder_1_out4), .out5(decoder_1_out5), .out6(decoder_1_out6), .out7(decoder_1_out7),
    .sel(Address__to_be_written[2:0]));
  and and_1 (and_1_out, decoder_1_out0, Enable__Written);
  and and_2 (and_2_out, decoder_1_out1, Enable__Written);
  and and_3 (and_3_out, decoder_1_out2, Enable__Written);
  and and_4 (and_4_out, decoder_1_out3, Enable__Written);
  and and_5 (and_5_out, decoder_1_out4, Enable__Written);
  and and_6 (and_6_out, decoder_1_out5, Enable__Written);
  and and_7 (and_7_out, decoder_1_out6, Enable__Written);
  and and_8 (and_8_out, decoder_1_out7, Enable__Written);
  Register register_1 (
    .D(Data__to_be_written), .en(and_1_out), .Q(register_1_q), .clk(Clock__value_update_on_trigger));  // open: clr
  Register register_2 (
    .D(Data__to_be_written), .en(and_2_out), .Q(register_2_q), .clk(Clock__value_update_on_trigger));  // open: clr
  Register register_3 (
    .D(Data__to_be_written), .en(and_3_out), .Q(register_3_q), .clk(Clock__value_update_on_trigger));  // open: clr
  Register register_4 (
    .D(Data__to_be_written), .en(and_4_out), .Q(register_4_q), .clk(Clock__value_update_on_trigger));  // open: clr
  Register register_5 (
    .D(Data__to_be_written), .en(and_5_out), .Q(register_5_q), .clk(Clock__value_update_on_trigger));  // open: clr
  Register register_6 (
    .D(Data__to_be_written), .en(and_6_out), .Q(register_6_q), .clk(Clock__value_update_on_trigger));  // open: clr
  Register register_7 (
    .D(Data__to_be_written), .en(and_7_out), .Q(register_7_q), .clk(Clock__value_update_on_trigger));  // open: clr
  Register register_8 (.D(Data__to_be_written), .en(and_8_out), .Q(register_8_q));  // open: clk, clr
  Multiplexer #(.select(3), .width(8), .enable("false")) multiplexer_1 (
    .in0(register_1_q), .in1(register_2_q), .in2(register_3_q), .in3(register_4_q), .in4(register_5_q),
    .in5(register_6_q), .in6(register_7_q), .in7(register_8_q), .out(Data__to_be_output0),
    .sel(Address__to_be_read0[2:0]));
  Multiplexer #(.select(3), .width(8), .enable("false")) multiplexer_2 (
    .in0(register_1_q), .in1(register_2_q), .in2(register_3_q), .in3(register_4_q), .in4(register_5_q),
    .in5(register_6_q), .in6(register_7_q), .in7(register_8_q), .out(Data__to_be_output1),
    .sel(Address__to_be_read1[2:0]));
endmodule

// Register Group
module RegisterGroup3 (
  input  [7:0] Data__to_be_written,
  input  [4:0] Address__to_be_read0,
  input  [4:0] Address__to_be_read1,
  input  [4:0] Address__to_be_written,
  input  Enable__Written,
  input  Clock__value_update_on_trigger,
  output [7:0] Data__to_be_output0,
  output [7:0] Data__to_be_output1,
  output [7:0] Data__R4,
  output [7:0] Data__R5,
  output [7:0] Data__R6
);

  wire and_1_out, and_2_out, and_3_out, and_4_out, and_5_out, and_6_out, and_7_out, and_8_out,
       decoder_1_out0, decoder_1_out1, decoder_1_out2, decoder_1_out3, decoder_1_out4, decoder_1_out5,
       decoder_1_out6, decoder_1_out7;
  wire [7:0] register_1_q, register_2_q, register_3_q, register_4_q, register_8_q;

  Decoder #(.select(3), .enable("false")) decoder_1 (
    .out0(decoder_1_out0), .out1(decoder_1_out1), .out2(decoder_1_out2), .out3(decoder_1_out3),
    .out4(decoder_1_out4), .out5(decoder_1_out5), .out6(decoder_1_out6), .out7(decoder_1_out7),
    .sel(Address__to_be_written[2:0]));
  and and_1 (and_1_out, decoder_1_out0, Enable__Written);
  and and_2 (and_2_out, decoder_1_out1, Enable__Written);
  and and_3 (and_3_out, decoder_1_out2, Enable__Written);
  and and_4 (and_4_out, decoder_1_out3, Enable__Written);
  and and_5 (and_5_out, decoder_1_out4, Enable__Written);
  and and_6 (and_6_out, decoder_1_out5, Enable__Written);
  and and_7 (and_7_out, decoder_1_out6, Enable__Written);
  and and_8 (and_8_out, decoder_1_out7, Enable__Written);
  Register register_1 (
    .D(Data__to_be_written), .en(and_1_out), .Q(register_1_q), .clk(Clock__value_update_on_trigger));  // open: clr
  Register register_2 (
    .D(Data__to_be_written), .en(and_2_out), .Q(register_2_q), .clk(Clock__value_update_on_trigger));  // open: clr
  Register register_3 (
    .D(Data__to_be_written), .en(and_3_out), .Q(register_3_q), .clk(Clock__value_update_on_trigger));  // open: clr
  Register register_4 (
    .D(Data__to_be_written), .en(and_4_out), .Q(register_4_q), .clk(Clock__value_update_on_trigger));  // open: clr
  Register register_5 (
    .D(Data__to_be_written), .en(and_5_out), .Q(Data__R4), .clk(Clock__value_update_on_trigger));  // open: clr
  Register register_6 (
    .D(Data__to_be_written), .en(and_6_out), .Q(Data__R5), .clk(Clock__value_update_on_trigger));  // open: clr
  Register register_7 (
    .D(Data__to_be_written), .en(and_7_out), .Q(Data__R6), .clk(Clock__value_update_on_trigger));  // open: clr
  Register register_8 (.D(Data__to_be_written), .en(and_8_out), .Q(register_8_q));  // open: clk, clr
  Multiplexer #(.select(3), .width(8), .enable("false")) multiplexer_1 (
    .in0(register_1_q), .in1(register_2_q), .in2(register_3_q), .in3(register_4_q), .in4(Data__R4),
    .in5(Data__R5), .in6(Data__R6), .in7(register_8_q), .out(Data__to_be_output0),
    .sel(Address__to_be_read0[2:0]));
  Multiplexer #(.select(3), .width(8), .enable("false")) multiplexer_2 (
    .in0(register_1_q), .in1(register_2_q), .in2(register_3_q), .in3(register_4_q), .in4(Data__R4),
    .in5(Data__R5), .in6(Data__R6), .in7(register_8_q), .out(Data__to_be_output1),
    .sel(Address__to_be_read1[2:0]));
endmodule

module CPU1 (
);

  wire clock_1_out, not_1_out;
  wire [7:0] alu_1_data__output_number, multiplexer_1_out, ram_1_data, registergroup1_1_data__to_be_output;

  Clock clock_1 (.out(clock_1_out));
  RegisterGroup1 registergroup1_1 (
    .Address__to_be_read(5'b00111), .Data__to_be_written(multiplexer_1_out),
    .Address__to_be_written({5{1'b0}}), .Enable__Written(1'b1), .Clock__value_update_on_trigger(clock_1_out),
    .Data__to_be_output(registergroup1_1_data__to_be_output));
  Multiplexer #(.width(8), .enable("false")) multiplexer_1 (
    .in0(alu_1_data__output_number), .in1(ram_1_data), .out(multiplexer_1_out), .sel(1'b0));
  ALU alu_1 (
    .Control__100x_LU__011x_AU(3'b110), .Data__input_number(registergroup1_1_data__to_be_output),
    .Data__input_number_2(8'h1), .Data__output_number(alu_1_data__output_number));
  not not_1 (not_1_out, 1'b0);
  RAM #(.bus("separate")) ram_1 (
    .addr(alu_1_data__output_number), .din(registergroup1_1_data__to_be_output), .data(ram_1_data),
    .str(1'b0), .clk(clock_1_out), .ld(not_1_out));  // open: sel, clr
endmodule

module CPU2 (
);

  wire clock_1_out, not_1_out;
  wire [7:0] alu_1_data__output_number, multiplexer_1_out, pc1_1_data__total_time, ram_1_data,
       registergroup2_1_data__to_be_output0, registergroup2_1_data__to_be_output1;
  wire [31:0] rom_1_data;

  Clock clock_1 (.out(clock_1_out));
  PC1 pc1_1 (.Clock__time_counter(clock_1_out), .Data__total_time(pc1_1_data__total_time));
  ROM #(.dataWidth(32)) rom_1 (.addr(pc1_1_data__total_time), .data(rom_1_data));  // open: sel
  RegisterGroup2 registergroup2_1 (
    .Address__to_be_read1(rom_1_data[20:16]), .Data__to_be_written(multiplexer_1_out),
    .Address__to_be_written(rom_1_data[20:16]), .Enable__Written(rom_1_data[31]),
    .Clock__value_update_on_trigger(clock_1_out), .Data__to_be_output0(registergroup2_1_data__to_be_output0),
    .Address__to_be_read0(rom_1_data[25:21]), .Data__to_be_output1(registergroup2_1_data__to_be_output1));
  Multiplexer #(.width(8), .enable("false")) multiplexer_1 (
    .in0(alu_1_data__output_number), .in1(ram_1_data), .out(multiplexer_1_out), .sel(rom_1_data[30]));
  ALU alu_1 (
    .Control__100x_LU__011x_AU(rom_1_data[2:0]), .Data__input_number(registergroup2_1_data__to_be_output0),
    .Data__input_number_2(rom_1_data[13:6]), .Data__output_number(alu_1_data__output_number));
  not not_1 (not_1_out, rom_1_data[29]);
  RAM #(.bus("separate")) ram_1 (
    .addr(alu_1_data__output_number), .din(registergroup2_1_data__to_be_output1), .data(ram_1_data),
    .str(rom_1_data[29]), .clk(clock_1_out), .ld(not_1_out));  // open: sel, clr

  // Notes on the sheet:
  //   contents of rom_1 (hex, n*v repeats v):
  //   80e00046 80e10106 20010006 20010046 c0040006 c0050046 80e60086 80e60106 c0010006 80210046 20010006
endmodule

// CPU
module CPU3 (
  input  Clock,
  output [7:0] Screen__x,
  output [7:0] Screen__y,
  output [7:0] Control
);

  wire not_1_out;
  wire [7:0] alu_1_data__output_number, bit_extender_1_out, multiplexer_1_out, pc2_1_data__total_time,
       ram_1_data, registergroup3_1_data__to_be_output0, registergroup3_1_data__to_be_output1;
  wire [31:0] rom_1_data;

  Bit_Extender #(.in_width(32), .out_width(8)) bit_extender_1 (.in(rom_1_data), .out(bit_extender_1_out));
  PC2 pc2_1 (
    .Clock__time_counter(Clock), .Data__total_time(pc2_1_data__total_time),
    .Jump__1_jump__2_normal(rom_1_data[28]), .Jump_position(bit_extender_1_out));
  ROM #(.dataWidth(32)) rom_1 (.addr(pc2_1_data__total_time), .data(rom_1_data));  // open: sel
  RegisterGroup3 registergroup3_1 (
    .Data__to_be_written(multiplexer_1_out), .Address__to_be_read0(rom_1_data[25:21]),
    .Address__to_be_read1(rom_1_data[20:16]), .Address__to_be_written(rom_1_data[20:16]),
    .Data__to_be_output0(registergroup3_1_data__to_be_output0),
    .Data__to_be_output1(registergroup3_1_data__to_be_output1), .Data__R4(Screen__x), .Data__R5(Screen__y),
    .Data__R6(Control), .Enable__Written(rom_1_data[31]), .Clock__value_update_on_trigger(Clock));
  Multiplexer #(.width(8), .enable("false")) multiplexer_1 (
    .in0(alu_1_data__output_number), .in1(ram_1_data), .out(multiplexer_1_out), .sel(rom_1_data[30]));
  ALU alu_1 (
    .Control__100x_LU__011x_AU(rom_1_data[2:0]), .Data__input_number(registergroup3_1_data__to_be_output0),
    .Data__input_number_2(rom_1_data[13:6]), .Data__output_number(alu_1_data__output_number));
  not not_1 (not_1_out, rom_1_data[29]);
  RAM #(.bus("separate")) ram_1 (
    .addr(alu_1_data__output_number), .din(registergroup3_1_data__to_be_output1), .data(ram_1_data),
    .str(rom_1_data[29]), .clk(Clock), .ld(not_1_out));  // open: sel, clr

  // Notes on the sheet:
  //   contents of rom_1 (hex, n*v repeats v):
  //   80e00046 80e10106 20010006 20010046 c0040006 c0050046 80e60046 80e60106 80e60086 c0010006 80210046
  //   20010006 c0040006 c0050046 80e60046 80e60106 80e60086 10000009
endmodule

// SRD
module ScreenRegsrDec (
  input  Input_0,
  input  Input_1,
  input  Input_2,
  input  Input_3,
  input  Input_4,
  input  Input_5,
  input  Input_6,
  input  Input_7,
  input  Input_0_2,
  input  Input_1_2,
  input  Input_2_2,
  input  Input_3_2,
  input  Input_4_2,
  input  Input_5_2,
  input  Input_6_2,
  input  Input_7_2,
  output [7:0] Output_0,
  output [7:0] Output_1,
  output [7:0] Output_2,
  output [7:0] Output_3,
  output [7:0] Output_4,
  output [7:0] Output_5,
  output [7:0] Output_6,
  output [7:0] Output_7
);

  and and_1 (Output_0[0], Input_0, Input_0_2);
  and and_2 (Output_1[0], Input_1, Input_0_2);
  and and_3 (Output_2[0], Input_2, Input_0_2);
  and and_4 (Output_3[0], Input_3, Input_0_2);
  and and_5 (Output_4[0], Input_4, Input_0_2);
  and and_6 (Output_5[0], Input_5, Input_0_2);
  and and_7 (Output_6[0], Input_6, Input_0_2);
  and and_8 (Output_7[0], Input_7, Input_0_2);
  and and_9 (Output_0[1], Input_0, Input_1_2);
  and and_10 (Output_1[1], Input_1, Input_1_2);
  and and_11 (Output_2[1], Input_2, Input_1_2);
  and and_12 (Output_3[1], Input_3, Input_1_2);
  and and_13 (Output_4[1], Input_4, Input_1_2);
  and and_14 (Output_5[1], Input_5, Input_1_2);
  and and_15 (Output_6[1], Input_6, Input_1_2);
  and and_16 (Output_7[1], Input_7, Input_1_2);
  and and_17 (Output_0[3], Input_0, Input_3_2);
  and and_18 (Output_0[2], Input_0, Input_2_2);
  and and_19 (Output_1[3], Input_1, Input_3_2);
  and and_20 (Output_1[2], Input_1, Input_2_2);
  and and_21 (Output_2[2], Input_2, Input_2_2);
  and and_22 (Output_2[3], Input_2, Input_3_2);
  and and_23 (Output_3[3], Input_3, Input_3_2);
  and and_24 (Output_3[2], Input_3, Input_2_2);
  and and_25 (Output_4[3], Input_4, Input_3_2);
  and and_26 (Output_4[2], Input_4, Input_2_2);
  and and_27 (Output_5[3], Input_5, Input_3_2);
  and and_28 (Output_5[2], Input_5, Input_2_2);
  and and_29 (Output_6[3], Input_6, Input_3_2);
  and and_30 (Output_6[2], Input_6, Input_2_2);
  and and_31 (Output_7[2], Input_7, Input_2_2);
  and and_32 (Output_7[3], Input_7, Input_3_2);
  and and_33 (Output_0[4], Input_0, Input_4_2);
  and and_34 (Output_1[4], Input_1, Input_4_2);
  and and_35 (Output_2[4], Input_2, Input_4_2);
  and and_36 (Output_3[4], Input_3, Input_4_2);
  and and_37 (Output_4[4], Input_4, Input_4_2);
  and and_38 (Output_5[4], Input_5, Input_4_2);
  and and_39 (Output_6[4], Input_6, Input_4_2);
  and and_40 (Output_7[4], Input_7, Input_4_2);
  and and_41 (Output_0[5], Input_0, Input_5_2);
  and and_42 (Output_1[5], Input_1, Input_5_2);
  and and_43 (Output_2[5], Input_2, Input_5_2);
  and and_44 (Output_3[5], Input_3, Input_5_2);
  and and_45 (Output_4[5], Input_4, Input_5_2);
  and and_46 (Output_5[5], Input_5, Input_5_2);
  and and_47 (Output_6[5], Input_6, Input_5_2);
  and and_48 (Output_7[5], Input_7, Input_5_2);
  and and_49 (Output_0[6], Input_0, Input_6_2);
  and and_50 (Output_0[7], Input_0, Input_7_2);
  and and_51 (Output_1[7], Input_1, Input_7_2);
  and and_52 (Output_1[6], Input_1, Input_6_2);
  and and_53 (Output_2[6], Input_2, Input_6_2);
  and and_54 (Output_2[7], Input_2, Input_7_2);
  and and_55 (Output_3[7], Input_3, Input_7_2);
  and and_56 (Output_3[6], Input_3, Input_6_2);
  and and_57 (Output_4[7], Input_4, Input_7_2);
  and and_58 (Output_4[6], Input_4, Input_6_2);
  and and_59 (Output_5[7], Input_5, Input_7_2);
  and and_60 (Output_5[6], Input_5, Input_6_2);
  and and_61 (Output_6[6], Input_6, Input_6_2);
  and and_62 (Output_6[7], Input_6, Input_7_2);
  and and_63 (Output_7[7], Input_7, Input_7_2);
  and and_64 (Output_7[6], Input_7, Input_6_2);
endmodule

// SD
module ScreenDecoder (
  input  [7:0] Input_x_label,
  input  [7:0] Input_y_label,
  input  Clock,
  input  Clear,
  input  Falsh,
  output [7:0] Output_0,
  output [7:0] Output_1,
  output [7:0] Output_2,
  output [7:0] Output_3,
  output [7:0] Output_4,
  output [7:0] Output_5,
  output [7:0] Output_6,
  output [7:0] Output_7
);

  wire demultiplexer_1_out0, demultiplexer_1_out1, demultiplexer_1_out2, demultiplexer_1_out3,
       demultiplexer_1_out4, demultiplexer_1_out5, demultiplexer_1_out6, demultiplexer_1_out7,
       demultiplexer_2_out0, demultiplexer_2_out1, demultiplexer_2_out2, demultiplexer_2_out4,
       demultiplexer_2_out5, demultiplexer_2_out6, demultiplexer_2_out7;
  wire [7:0] register_2_q, register_3_q, register_6_q, register_8_q, register_9_q, register_12_q,
       register_14_q, register_15_q, screenregsrdec_1_output_0, screenregsrdec_1_output_1,
       screenregsrdec_1_output_2, screenregsrdec_1_output_3, screenregsrdec_1_output_4,
       screenregsrdec_1_output_5, screenregsrdec_1_output_6, screenregsrdec_1_output_7;

  Demultiplexer #(.select(3), .enable("false")) demultiplexer_1 (
    .out0(demultiplexer_1_out0), .out1(demultiplexer_1_out1), .out2(demultiplexer_1_out2),
    .out3(demultiplexer_1_out3), .out4(demultiplexer_1_out4), .out5(demultiplexer_1_out5),
    .out6(demultiplexer_1_out6), .out7(demultiplexer_1_out7), .in(1'b1), .sel(Input_x_label[2:0]));
  Demultiplexer #(.select(3), .enable("false")) demultiplexer_2 (
    .out0(demultiplexer_2_out0), .out1(demultiplexer_2_out1), .out2(demultiplexer_2_out2),
    .out3(demultiplexer_2_out2), .out4(demultiplexer_2_out4), .out5(demultiplexer_2_out5),
    .out6(demultiplexer_2_out6), .out7(demultiplexer_2_out7), .in(1'b1), .sel(Input_y_label[2:0]));
  ScreenRegsrDec screenregsrdec_1 (
    .Input_0(demultiplexer_1_out0), .Input_1(demultiplexer_1_out1), .Input_2(demultiplexer_1_out2),
    .Input_3(demultiplexer_1_out3), .Input_4(demultiplexer_1_out4), .Input_5(demultiplexer_1_out5),
    .Input_6(demultiplexer_1_out6), .Input_7(demultiplexer_1_out7), .Output_0(screenregsrdec_1_output_0),
    .Output_1(screenregsrdec_1_output_1), .Output_2(screenregsrdec_1_output_2),
    .Output_3(screenregsrdec_1_output_3), .Output_4(screenregsrdec_1_output_4),
    .Output_5(screenregsrdec_1_output_5), .Output_6(screenregsrdec_1_output_6),
    .Output_7(screenregsrdec_1_output_7), .Input_0_2(demultiplexer_2_out0), .Input_1_2(demultiplexer_2_out1),
    .Input_2_2(demultiplexer_2_out2), .Input_3_2(demultiplexer_2_out2), .Input_4_2(demultiplexer_2_out4),
    .Input_5_2(demultiplexer_2_out5), .Input_6_2(demultiplexer_2_out6), .Input_7_2(demultiplexer_2_out7));
  Register #(.width(1)) register_1 (
    .D(1'b1), .en(screenregsrdec_1_output_0[1]), .Q(register_2_q[1]), .clk(Clock), .clr(Clear));
  Register #(.width(1)) register_2 (
    .D(1'b1), .en(screenregsrdec_1_output_0[0]), .Q(register_2_q[0]), .clk(Clock), .clr(Clear));
  Register #(.width(1)) register_3 (
    .D(1'b1), .en(screenregsrdec_1_output_1[0]), .Q(register_3_q[0]), .clk(Clock), .clr(Clear));
  Register #(.width(1)) register_4 (
    .D(1'b1), .en(screenregsrdec_1_output_1[1]), .Q(register_3_q[1]), .clk(Clock), .clr(Clear));
  Register #(.width(1)) register_5 (
    .D(1'b1), .en(screenregsrdec_1_output_2[1]), .Q(register_6_q[1]), .clk(Clock), .clr(Clear));
  Register #(.width(1)) register_6 (
    .D(1'b1), .en(screenregsrdec_1_output_2[0]), .Q(register_6_q[0]), .clk(Clock), .clr(Clear));
  Register #(.width(1)) register_7 (
    .D(1'b1), .en(screenregsrdec_1_output_3[1]), .Q(register_8_q[1]), .clk(Clock), .clr(Clear));
  Register #(.width(1)) register_8 (
    .D(1'b1), .en(screenregsrdec_1_output_3[0]), .Q(register_8_q[0]), .clk(Clock), .clr(Clear));
  Register #(.width(1)) register_9 (
    .D(1'b1), .en(screenregsrdec_1_output_4[0]), .Q(register_9_q[0]), .clk(Clock), .clr(Clear));
  Register #(.width(1)) register_10 (
    .D(1'b1), .en(screenregsrdec_1_output_4[1]), .Q(register_9_q[1]), .clk(Clock), .clr(Clear));
  Register #(.width(1)) register_11 (
    .D(1'b1), .en(screenregsrdec_1_output_5[1]), .Q(register_12_q[1]), .clk(Clock), .clr(Clear));
  Register #(.width(1)) register_12 (
    .D(1'b1), .en(screenregsrdec_1_output_5[0]), .Q(register_12_q[0]), .clk(Clock), .clr(Clear));
  Register #(.width(1)) register_13 (
    .D(1'b1), .en(screenregsrdec_1_output_6[1]), .Q(register_14_q[1]), .clk(Clock), .clr(Clear));
  Register #(.width(1)) register_14 (
    .D(1'b1), .en(screenregsrdec_1_output_6[0]), .Q(register_14_q[0]), .clk(Clock), .clr(Clear));
  Register #(.width(1)) register_15 (
    .D(1'b1), .en(screenregsrdec_1_output_7[0]), .Q(register_15_q[0]), .clk(Clock), .clr(Clear));
  Register #(.width(1)) register_16 (
    .D(1'b1), .en(screenregsrdec_1_output_7[1]), .Q(register_15_q[1]), .clk(Clock), .clr(Clear));
  Register #(.width(1)) register_17 (
    .D(1'b1), .en(screenregsrdec_1_output_0[2]), .Q(register_2_q[2]), .clk(Clock), .clr(Clear));
  Register #(.width(1)) register_18 (
    .D(1'b1), .en(screenregsrdec_1_output_1[2]), .Q(register_3_q[2]), .clk(Clock), .clr(Clear));
  Register #(.width(1)) register_19 (
    .D(1'b1), .en(screenregsrdec_1_output_2[2]), .Q(register_6_q[2]), .clk(Clock), .clr(Clear));
  Register #(.width(1)) register_20 (
    .D(1'b1), .en(screenregsrdec_1_output_3[2]), .Q(register_8_q[2]), .clk(Clock), .clr(Clear));
  Register #(.width(1)) register_21 (
    .D(1'b1), .en(screenregsrdec_1_output_4[2]), .Q(register_9_q[2]), .clk(Clock), .clr(Clear));
  Register #(.width(1)) register_22 (
    .D(1'b1), .en(screenregsrdec_1_output_5[2]), .Q(register_12_q[2]), .clk(Clock), .clr(Clear));
  Register #(.width(1)) register_23 (
    .D(1'b1), .en(screenregsrdec_1_output_6[2]), .Q(register_14_q[2]), .clk(Clock), .clr(Clear));
  Register #(.width(1)) register_24 (
    .D(1'b1), .en(screenregsrdec_1_output_7[2]), .Q(register_15_q[2]), .clk(Clock), .clr(Clear));
  Register #(.width(1)) register_25 (
    .D(1'b1), .en(screenregsrdec_1_output_0[3]), .Q(register_2_q[3]), .clk(Clock), .clr(Clear));
  Register #(.width(1)) register_26 (
    .D(1'b1), .en(screenregsrdec_1_output_1[3]), .Q(register_3_q[3]), .clk(Clock), .clr(Clear));
  Register #(.width(1)) register_27 (
    .D(1'b1), .en(screenregsrdec_1_output_2[3]), .Q(register_6_q[3]), .clk(Clock), .clr(Clear));
  Register #(.width(1)) register_28 (
    .D(1'b1), .en(screenregsrdec_1_output_3[3]), .Q(register_8_q[3]), .clk(Clock), .clr(Clear));
  Register #(.width(1)) register_29 (
    .D(1'b1), .en(screenregsrdec_1_output_4[3]), .Q(register_9_q[3]), .clk(Clock), .clr(Clear));
  Register #(.width(1)) register_30 (
    .D(1'b1), .en(screenregsrdec_1_output_5[3]), .Q(register_12_q[3]), .clk(Clock), .clr(Clear));
  Register #(.width(1)) register_31 (
    .D(1'b1), .en(screenregsrdec_1_output_6[3]), .Q(register_14_q[3]), .clk(Clock), .clr(Clear));
  Register #(.width(1)) register_32 (
    .D(1'b1), .en(screenregsrdec_1_output_7[3]), .Q(register_15_q[3]), .clk(Clock), .clr(Clear));
  Register #(.width(1)) register_33 (
    .D(1'b1), .en(screenregsrdec_1_output_0[5]), .Q(register_2_q[5]), .clk(Clock), .clr(Clear));
  Register #(.width(1)) register_34 (
    .D(1'b1), .en(screenregsrdec_1_output_0[4]), .Q(register_2_q[4]), .clk(Clock), .clr(Clear));
  Register #(.width(1)) register_35 (
    .D(1'b1), .en(screenregsrdec_1_output_1[5]), .Q(register_3_q[5]), .clk(Clock), .clr(Clear));
  Register #(.width(1)) register_36 (
    .D(1'b1), .en(screenregsrdec_1_output_1[4]), .Q(register_3_q[4]), .clk(Clock), .clr(Clear));
  Register #(.width(1)) register_37 (
    .D(1'b1), .en(screenregsrdec_1_output_2[4]), .Q(register_6_q[4]), .clk(Clock), .clr(Clear));
  Register #(.width(1)) register_38 (
    .D(1'b1), .en(screenregsrdec_1_output_2[5]), .Q(register_6_q[5]), .clk(Clock), .clr(Clear));
  Register #(.width(1)) register_39 (
    .D(1'b1), .en(screenregsrdec_1_output_3[4]), .Q(register_8_q[4]), .clk(Clock), .clr(Clear));
  Register #(.width(1)) register_40 (
    .D(1'b1), .en(screenregsrdec_1_output_3[5]), .Q(register_8_q[5]), .clk(Clock), .clr(Clear));
  Register #(.width(1)) register_41 (
    .D(1'b1), .en(screenregsrdec_1_output_4[5]), .Q(register_9_q[5]), .clk(Clock), .clr(Clear));
  Register #(.width(1)) register_42 (
    .D(1'b1), .en(screenregsrdec_1_output_4[4]), .Q(register_9_q[4]), .clk(Clock), .clr(Clear));
  Register #(.width(1)) register_43 (
    .D(1'b1), .en(screenregsrdec_1_output_5[4]), .Q(register_12_q[4]), .clk(Clock), .clr(Clear));
  Register #(.width(1)) register_44 (
    .D(1'b1), .en(screenregsrdec_1_output_5[5]), .Q(register_12_q[5]), .clk(Clock), .clr(Clear));
  Register #(.width(1)) register_45 (
    .D(1'b1), .en(screenregsrdec_1_output_6[5]), .Q(register_14_q[5]), .clk(Clock), .clr(Clear));
  Register #(.width(1)) register_46 (
    .D(1'b1), .en(screenregsrdec_1_output_6[4]), .Q(register_14_q[4]), .clk(Clock), .clr(Clear));
  Register #(.width(1)) register_47 (
    .D(1'b1), .en(screenregsrdec_1_output_7[4]), .Q(register_15_q[4]), .clk(Clock), .clr(Clear));
  Register #(.width(1)) register_48 (
    .D(1'b1), .en(screenregsrdec_1_output_7[5]), .Q(register_15_q[5]), .clk(Clock), .clr(Clear));
  Register #(.width(1)) register_49 (
    .D(1'b1), .en(screenregsrdec_1_output_0[6]), .Q(register_2_q[6]), .clk(Clock), .clr(Clear));
  Register #(.width(1)) register_50 (
    .D(1'b1), .en(screenregsrdec_1_output_1[6]), .Q(register_3_q[6]), .clk(Clock), .clr(Clear));
  Register #(.width(1)) register_51 (
    .D(1'b1), .en(screenregsrdec_1_output_2[6]), .Q(register_6_q[6]), .clk(Clock), .clr(Clear));
  Register #(.width(1)) register_52 (
    .D(1'b1), .en(screenregsrdec_1_output_3[6]), .Q(register_8_q[6]), .clk(Clock), .clr(Clear));
  Register #(.width(1)) register_53 (
    .D(1'b1), .en(screenregsrdec_1_output_4[6]), .Q(register_9_q[6]), .clk(Clock), .clr(Clear));
  Register #(.width(1)) register_54 (
    .D(1'b1), .en(screenregsrdec_1_output_5[6]), .Q(register_12_q[6]), .clk(Clock), .clr(Clear));
  Register #(.width(1)) register_55 (
    .D(1'b1), .en(screenregsrdec_1_output_6[6]), .Q(register_14_q[6]), .clk(Clock), .clr(Clear));
  Register #(.width(1)) register_56 (
    .D(1'b1), .en(screenregsrdec_1_output_7[6]), .Q(register_15_q[6]), .clk(Clock), .clr(Clear));
  Register #(.width(1)) register_57 (
    .D(1'b1), .en(screenregsrdec_1_output_0[7]), .Q(register_2_q[7]), .clk(Clock), .clr(Clear));
  Register #(.width(1)) register_58 (
    .D(1'b1), .en(screenregsrdec_1_output_1[7]), .Q(register_3_q[7]), .clk(Clock), .clr(Clear));
  Register #(.width(1)) register_59 (
    .D(1'b1), .en(screenregsrdec_1_output_2[7]), .Q(register_6_q[7]), .clk(Clock), .clr(Clear));
  Register #(.width(1)) register_60 (
    .D(1'b1), .en(screenregsrdec_1_output_3[7]), .Q(register_8_q[7]), .clk(Clock), .clr(Clear));
  Register #(.width(1)) register_61 (
    .D(1'b1), .en(screenregsrdec_1_output_4[7]), .Q(register_9_q[7]), .clk(Clock), .clr(Clear));
  Register #(.width(1)) register_62 (
    .D(1'b1), .en(screenregsrdec_1_output_5[7]), .Q(register_12_q[7]), .clk(Clock), .clr(Clear));
  Register #(.width(1)) register_63 (
    .D(1'b1), .en(screenregsrdec_1_output_6[7]), .Q(register_14_q[7]), .clk(Clock), .clr(Clear));
  Register #(.width(1)) register_64 (
    .D(1'b1), .en(screenregsrdec_1_output_7[7]), .Q(register_15_q[7]), .clk(Clock), .clr(Clear));
  Register register_65 (.D(register_2_q), .Q(Output_0), .clk(Falsh));  // open: en, clr
  Register register_66 (.D(register_3_q), .Q(Output_1), .clk(Falsh));  // open: en, clr
  Register register_67 (.D(register_6_q), .Q(Output_2), .clk(Falsh));  // open: en, clr
  Register register_68 (.D(register_8_q), .Q(Output_3), .clk(Falsh));  // open: en, clr
  Register register_69 (.D(register_9_q), .Q(Output_4), .clk(Falsh));  // open: en, clr
  Register register_70 (.D(register_12_q), .Q(Output_5), .clk(Falsh));  // open: en, clr
  Register register_71 (.D(register_14_q), .Q(Output_6), .clk(Falsh));  // open: en, clr
  Register register_72 (.D(register_15_q), .Q(Output_7), .clk(Falsh));  // open: en, clr
endmodule
